// Logisim project onBitALU.circ as structural Verilog: 1 circuit, main circuit main
module main (
  input  in_1,
  input  in_2,
  input  in_3,
  input  [1:0] in_4,
  output out_5,
  output out_6
);

  wire adder_1_out, and_1_out, or_1_out, xor_1_out;

  Adder #(.width(1)) adder_1 (.a(in_1), .b(in_3), .out(adder_1_out), .cin(in_2), .cout(out_5));
  and and_1 (and_1_out, in_1, in_3);
  or or_1 (or_1_out, in_1, in_3);
  xor xor_1 (xor_1_out, in_1, in_3);
  Multiplexer #(.select(2)) multiplexer_1 (
    .in0(adder_1_out), .in1(and_1_out), .in2(or_1_out), .in3(xor_1_out), .out(out_6), .sel(in_4));  // open: en
endmodule
