// Logisim project ranjan.circ as structural Verilog: 1 circuit, main circuit main
module main (
  input  in_1,
  input  in_2,
  output out_3
);

  xor xor_1 (out_3, in_1, in_2);
  // AND_Gate and_1 has open pins: in0=in_1, in3=in_2, out=open
endmodule
