// Logisim project three_is_to_eight_decoder.circ as structural Verilog: 1 circuit, main circuit main
module main (
  input  A0,
  input  A1,
  input  A2,
  input  E,
  output Y0,
  output Y1,
  output Y2,
  output Y3,
  output Y4,
  output Y5,
  output Y6,
  output Y7
);

  wire not_1_out, not_2_out, not_3_out;

  not not_1 (not_1_out, A0);
  not not_2 (not_2_out, A1);
  not not_3 (not_3_out, A2);
  and and_1 (Y0, E, not_3_out, not_2_out, not_1_out);
  and and_2 (Y1, E, A2, not_2_out, not_1_out);
  and and_3 (Y2, E, not_3_out, A1, not_1_out);
  and and_4 (Y3, E, A2, A1, not_1_out);
  and and_5 (Y4, E, not_3_out, not_2_out, A0);
  and and_6 (Y5, E, A2, not_2_out, A0);
  and and_7 (Y6, E, not_3_out, A1, A0);
  and and_8 (Y7, E, A2, A1, A0);
endmodule
