// Logisim project two_bit_array_multiplier.circ as structural Verilog: 1 circuit, main circuit main
module main (
  input  in_1,
  input  in_2,
  input  in_3,
  input  in_4,
  input  in_5,
  input  in_6,
  output out_7,
  output out_8,
  output out_9,
  output out_10
);

  wire adder_2_cout, and_1_out, and_2_out, and_3_out;

  and and_1 (and_1_out, in_5, in_4);
  Adder #(.width(1)) adder_1 (.a(adder_2_cout), .b(and_1_out), .out(out_10), .cout(out_9));  // open: cin
  and and_2 (and_2_out, in_3, in_1);
  and and_3 (and_3_out, in_5, in_6);
  Adder #(.width(1)) adder_2 (.a(and_2_out), .b(and_3_out), .out(out_7), .cout(adder_2_cout));  // open: cin
  and and_4 (out_8, in_3, in_2);

  // Notes on the sheet:
  //   2 Bit by 2 bit Array Multiplier
endmodule
